# Fritzing sketch breadboard_homedevice (saved by Fritzing 0.9.4)
circuit board: 5.11699cm x 5.23045cm
breadboards: 1

parts:
  S1 = SWITCH-MOMENTARY-2 [package=tactile-pth-12mm]
  SG1 = Buzzer 12mm [package=buzzer-ccv]
  ESP8266_NodeMCU_v1_0 = NodeMCU V1.0

nets:
  N1: S1.1, ESP8266_NodeMCU_v1_0.D6
  N2: S1.2, SG1.1, ESP8266_NodeMCU_v1_0.GND
  N3: SG1.2, ESP8266_NodeMCU_v1_0.D2

notes:
  Vehicle Anti-Theft Alarm: Home Device

custom parts:
  NodeMCU V1.0: ESP8266 based NodeMCU
