# Fritzing sketch breadboard_vehicledevice (saved by Fritzing 0.9.4)
circuit board: 5.273cm x 5.41109cm
breadboards: 1

parts:
  ESP8266_NodeMCU_v1_0 = NodeMCU V1.0
  9V = Battery block 9V
  LIS3DH = Adafruit LIS3DH Triple-Axis Accelerometer [part_number="Adafruit #2809"]

nets:
  N1: ESP8266_NodeMCU_v1_0.D1, LIS3DH.SCL
  N2: ESP8266_NodeMCU_v1_0.D2, LIS3DH.SDA
  3V3: ESP8266_NodeMCU_v1_0.3V3, LIS3DH.VCC
  GND: ESP8266_NodeMCU_v1_0.GND, 9V.-, LIS3DH.GND
  N3: ESP8266_NodeMCU_v1_0.Vin, 9V.+

notes:
  +
  -
  Vehicle Anti-Theft Sensor: Vehicle Device

custom parts:
  NodeMCU V1.0: ESP8266 based NodeMCU
  Adafruit LIS3DH Triple-Axis Accelerometer: The LIS3DH is a very popular low power triple-axis accelerometer. It's low-cost, but has just about every 'extra' you'd want in an accelerometer: Three axis sensing, 10-bit precision ±2g/±4g/±8g/±16g selectable scaling Both I2C (2 possible addresses) and SPI interface options Interrupt output Multiple data rate options 1 Hz to 5Khz As low as 2uA current draw (just the chip itself, not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
